# Fritzing sketch Type-X (saved by Fritzing 0.9.3b)
circuit board: 6.8cm x 15.8cm
breadboards: 2

parts:
  Vcc+ = Header 1 [package=1x01_offset]
  MoIC2 = TA7291P [package=HSIP10-P-2.54(THT)]
  M1 = DC Motor
  S1 = SWITCH-MOMENTARY-2 [package=tactile-pth]
  CPU = Arduino Nano (Rev3.0)
  MoIC1 = TA7291P [package=HSIP10-P-2.54(THT)]
  M2 = DC Motor
  PW = female pin header, 3 pins [form="♀ (female)"]
  Gnd- = Header 1 [package=1x01_offset]
  Bt1 = female pin header, 4 pins [form="♀ (female)"]
  VCC1 = 4 x AAA Battery Mount

nets:
  N1: Vcc+.1, PW.pin1, VCC1.+
  GND: MoIC2.GND, S1.2, CPU.GND, MoIC1.GND, Gnd-.1, Bt1.pin3, VCC1.-
  N2: MoIC2.OUT1, M2.pin_1
  N3: MoIC2.Vref, CPU.D3
  N4: MoIC2.IN1, CPU.D7
  N5: MoIC2.IN2, CPU.D6
  N6: MoIC2.Vs, CPU.VIN, MoIC1.Vs, PW.pin2
  N7: MoIC2.OUT2, M2.pin_2
  N8: M1.pin_1, MoIC1.OUT1
  N9: M1.pin_2, MoIC1.OUT2
  N10: S1.1, CPU.D10, Bt1.pin2
  N11: CPU.D5, MoIC1.Vref
  N12: CPU.D8, MoIC1.IN2
  N13: CPU.D9, MoIC1.IN1
  N14: CPU.D11/MOSI, Bt1.pin1
  N15: CPU.5V, Bt1.pin4

notes:
  O
  Type-X_Ver.1.0
  I

custom parts:
  TA7291P: The IC are Full-Bridge Driver. 4 modes available (CW / CCW / STOP / BRAKE) and PWM control. Output current:1.0 A (AVE.) 2.0 A (PEAK)
