# Fritzing sketch spica (saved by Fritzing 0.9.3b)
circuit board: 5.80282cm x 6.28259cm
breadboards: 1

parts:
  IC1 = V_REG_LD1117VXX [package=78xxl]
  C1 = Ceramic Capacitor [capacitance=0.1µF voltage=6.3V package="100 mil [THT, multilayer]"]
  C2 = Electrolytic Capacitor [capacitance=100µF package="100 mil [THT, electrolytic]"]
  C3 = Electrolytic Capacitor [capacitance=1mF voltage=10V package="100 mil [THT, electrolytic]"]
  IC2 = AE-DRV8835-S [package="DIP (Dual Inline) [THT]"]
  M2 = DC Motor
  M1 = DC Motor
  VCC2 = Battery
  S1 = Toggle Switch [package=THT]
  JP8 = Header 4 [package=molex-1x4_lock]
  J2 = female pin header, 3 pins [form="♀ (female)"]
  U1 = ESP32S-HiLetgo [part_number=ESP32S-HiLetgo]

nets:
  N1: IC1.OUT, C2.+, IC2.MODE, IC2.VCC, J2.pin3, U1.3.3
  GND: IC1.GND, C1.0, C2.-, C3.-, IC2.GND, VCC2.-, JP8.1, J2.pin2, U1.GND
  N2: IC1.IN, C1.1, C3.+, IC2.VM, S1.L2
  N3: IC2.AOUT1, M1.pin_1
  N4: IC2.AOUT2, M1.pin_2
  N5: IC2.BOUT1, M2.pin_1
  N6: IC2.BOUT2, M2.pin_2
  N7: IC2.BIN2, U1.GPIO17
  N8: IC2.BIN1, U1.GPIO16
  N9: IC2.AIN2, U1.GPIO26
  N10: IC2.AIN1, U1.GPIO25
  N11: VCC2.+, S1.COM
  N12: JP8.2, U1.GPIO23
  N13: JP8.3, U1.GPIO22
  N14: JP8.4, J2.pin1

notes:
  USB
  Spica Dev Rev1.0b

custom parts:
  AE-DRV8835-S: A DRV8835 breakout board by Akizuki Denshi Tsusho Co.,Ltd.
  ESP32S-HiLetgo: HiLetgo ESP-WROOM-32 ESP32 ESP-32S Development Board 2.4GHz Dual-Mode WiFi + Bluetooth Dual Cores Microcontroller The ESP32 integrated with Antenna switches, RF Balun, power amplifiers, low-noise amplifiers, filters, and management modules, and the entire solution occupies the least area of PCB. 2.4 GHz Wi-Fi plus Bluetooth dual-mode chip, with TSMC Ultra-low power consumption 40nm technology,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
