# Fritzing sketch spica (saved by Fritzing 0.9.3b)
circuit board: 5.80282cm x 6.28259cm
breadboards: 1

parts:
  IC1 = V_REG_LD1117VXX [package=78xxl]
  C1 = Ceramic Capacitor [capacitance=0.1µF voltage=6.3V package="100 mil [THT, multilayer]"]
  C2 = Electrolytic Capacitor [capacitance=100µF package="100 mil [THT, electrolytic]"]
  C3 = Electrolytic Capacitor [capacitance=1mF voltage=10V package="100 mil [THT, electrolytic]"]
  IC2 = AE-DRV8835-S [package="DIP (Dual Inline) [THT]"]
  R1 = Resistor [tolerance=±5% resistance=220 package=THT]
  M2 = DC Motor
  R2 = Trimmer Potentiometer [maximum_resistance=10kΩ package=THT]
  M1 = DC Motor
  JP2 = M16 [package=1x16_machine-pin-header_lock.004]
  JP3 = Header 3 [package=molex-1x3_lock]
  JP4 = M16 [package=1x16_machine-pin-header_lock.004]
  JP5 = M16 [package=1x16_machine-pin-header_lock.004]
  JP6 = Header 3 [package=molex-1x3_lock]
  JP7 = Header 3 [package=molex-1x3_lock]
  VCC2 = Battery
  S1 = Toggle Switch [package=THT]
  JP8 = Header 4 [package=molex-1x4_lock]
  J2 = female pin header, 3 pins [form="♀ (female)"]
  U1 = ESP32S-HiLetgo [part_number=ESP32S-HiLetgo]

nets:
  N1: IC1.OUT, C2.+, IC2.MODE, IC2.VCC, JP7.1, J2.pin3, U1.3.3
  GND: IC1.GND, C1.0, C2.-, C3.-, IC2.GND, JP2.4, JP3.1, JP4.6, JP5.4, JP6.1, VCC2.-, JP8.1, J2.pin2, U1.GND
  N2: IC1.IN, C1.1, C3.+, R1.Pin_1
  N3: IC2.VM, R1.Pin_0, S1.L2
  N4: IC2.AOUT1, M1.pin_1
  N5: IC2.AOUT2, M1.pin_2
  N6: IC2.BOUT1, M2.pin_1
  N7: IC2.BOUT2, M2.pin_2
  N8: IC2.BIN2, JP2.8, JP5.8, U1.GPIO17
  N9: IC2.BIN1, JP2.9, JP5.9, U1.GPIO16
  N10: IC2.AIN2, JP4.10, U1.GPIO26
  N11: IC2.AIN1, JP4.11, U1.GPIO25
  N12: R2.leg1, JP4.15, U1.GPIO34
  N13: R2.wiper, JP4.12, U1.GPIO33
  N14: R2.leg2, JP4.13, U1.GPIO32
  N15: JP2.1, JP5.1, U1.GPIO1
  N16: JP2.2, JP5.2, U1.GPIO3
  N17: JP2.3, JP5.3, U1.GPIO21
  N18: JP2.5, JP5.5, U1.GPIO19
  N19: JP2.6, JP5.6, U1.GPIO18
  N20: JP2.7, JP5.7, U1.GPIO5
  N21: JP2.10, JP5.10, U1.GPIO4
  N22: JP2.11, JP5.11, U1.GPIO0
  N23: JP2.12, JP5.12, U1.GPIO2
  N24: JP2.13, JP5.13, U1.GPIO15
  N25: JP2.14, JP5.14, U1.GPIO8
  N26: JP2.15, JP5.15, U1.GPIO7
  N27: JP2.16, JP5.16, U1.GPIO6
  N28: JP3.2, JP6.2, JP8.2, U1.GPIO23
  N29: JP3.3, JP6.3, JP8.3, U1.GPIO22
  N30: JP4.1, U1.VIN
  N31: JP4.2, U1.GPIO11
  N32: JP4.3, U1.GPIO10
  N33: JP4.4, U1.GPIO9
  N34: JP4.5, U1.GPIO13
  N35: JP4.7, U1.GPIO12
  N36: JP4.8, U1.GPIO14
  N37: JP4.9, U1.GPIO27
  N38: JP4.14, U1.GPIO35
  N39: JP4.16, U1.GPIO39
  N40: JP7.2, U1.EN
  N41: JP7.3, U1.GPIO36
  N42: VCC2.+, S1.COM
  N43: JP8.4, J2.pin1

notes:
  USB
  Spica Dev Rev1.0b

custom parts:
  AE-DRV8835-S: A DRV8835 breakout board by Akizuki Denshi Tsusho Co.,Ltd.
  ESP32S-HiLetgo: HiLetgo ESP-WROOM-32 ESP32 ESP-32S Development Board 2.4GHz Dual-Mode WiFi + Bluetooth Dual Cores Microcontroller The ESP32 integrated with Antenna switches, RF Balun, power amplifiers, low-noise amplifiers, filters, and management modules, and the entire solution occupies the least area of PCB. 2.4 GHz Wi-Fi plus Bluetooth dual-mode chip, with TSMC Ultra-low power consumption 40nm technology,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
